// Logisim project 20120298.circ as structural Verilog: 1 circuit, main circuit main
module main (
  input  I3,
  input  I2,
  input  I1,
  input  I0
);

  wire D0_out, D1_out, D2_out, D3_out, D4_out, D5_out, D6_out, I0_nI1I2_out, I0I1_out, I0I2_out, I1_nI2_out,
       nI0_nI1_out, nI0_nI2_out, nI0I1_out, nI0I2_out, nI1I2_out, not_1_out, not_2_out, not_3_out;

  and I0I2 (I0I2_out, I0, I2);
  and nI0I2 (nI0I2_out, I2, not_2_out);
  or D0 (D0_out, nI0I1_out, nI0_nI2_out, I1_nI2_out, I0_nI1I2_out, I3);
  not not_1 (not_1_out, I2);
  or D1 (D1_out, I2, not_3_out, I0);
  not not_2 (not_2_out, I0);
  not not_3 (not_3_out, I1);
  and nI0I1 (nI0I1_out, I1, not_2_out);
  and I0I1 (I0I1_out, I1, I0);
  or D2 (D2_out, nI0I1_out, nI0_nI2_out);
  and nI1I2 (nI1I2_out, not_3_out, I2);
  or D3 (D3_out, nI1I2_out, I3, nI0I1_out, I1_nI2_out);
  _7_Segment_Display u_7_segment_display_1 (
    .g(D3_out), .f(D5_out), .a(D6_out), .b(D4_out), .e(D2_out), .d(D0_out), .c(D1_out));  // open: dp
  and nI0_nI2 (nI0_nI2_out, not_1_out, not_2_out);
  or D4 (D4_out, not_1_out, I0I1_out, nI0_nI1_out);
  and I1_nI2 (I1_nI2_out, not_1_out, I1);
  or D5 (D5_out, nI1I2_out, nI0I2_out, nI0_nI1_out, I3);
  and nI0_nI1 (nI0_nI1_out, not_3_out, not_2_out);
  and I0_nI1I2 (I0_nI1I2_out, not_3_out, I2, I0);
  or D6 (D6_out, I0I2_out, I1, I3, nI0_nI2_out);
endmodule
